# Fritzing sketch Main circut diagram (saved by Fritzing 0.9.3b)
breadboards: 1

parts:
  Raspberry_Pi_1 = Raspberry Pi 3 [part_number=RPI-3-V1.2]
  Onderdeel1 = Arduino Uno (Rev3)
  S1 = H-Bridge with L298N
  M1 = DC Motor
  M2 = DC Motor
  Power_plug1 = Power plug
  hc-sr1 = hc-sr04
  hc-sr2 = hc-sr04
  Onderdeel2 = Adafruit Ultimate GPS v3 [part_number="Adafruit #746"]
  Onderdeel3 = 9-DOF Absolute Orientation IMU Fusion Breakout - BNO055

nets:
  N1: Raspberry_Pi_1.GPIO2, Onderdeel1.A4/SDA
  N2: Raspberry_Pi_1.GPIO3, Onderdeel1.A5/SCL
  GND: Raspberry_Pi_1.GND, Onderdeel1.GND, hc-sr1.GND, hc-sr2.GND, Onderdeel2.GND, Onderdeel3.GND
  N3: Raspberry_Pi_1.GPIO18, Onderdeel2.RX
  N4: Raspberry_Pi_1.GPIO15, Onderdeel2.TX
  5V: Raspberry_Pi_1.5V, Onderdeel2.VIN
  N5: Onderdeel1.D8, S1.IN1
  N6: Onderdeel1.D9_PWM, S1.IN2
  N7: Onderdeel1.D10_PWM/SS, hc-sr1.Trig
  N8: Onderdeel1.D11_PWM/MOSI, hc-sr1.Echo
  N9: Onderdeel1.D12/MISO, hc-sr2.Trig
  N10: Onderdeel1.D13/SCK, hc-sr2.Echo
  N11: Onderdeel1.D4, S1.IN4
  N12: Onderdeel1.D5_PWM, S1.ENB
  N13: Onderdeel1.D6_PWM, S1.ENA
  N14: Onderdeel1.D7, S1.IN3
  VCC: Onderdeel1.5V, hc-sr1.VCC, hc-sr2.VCC, Onderdeel3.5.0V
  12V: S1.12V, Power_plug1.VCC
  GND_2: S1.GND, Power_plug1.GND
  N15: S1.M1-01, M1.pin_2
  N16: S1.M1-02, M1.pin_1
  N17: S1.M2-01, M2.pin_2
  N18: S1.M2-02, M2.pin_1

notes:
  Arduino is powerd by 12v
  Raspberry pi is powerd by 5,4v
  Powerd by 12v buck boost converter

custom parts:
  H-Bridge with L298N: h-bridge
  Adafruit Ultimate GPS v3: We carry a few different GPS modules here in the Adafruit shop, but none that satisfied our every desire - that's why we designed this little GPS breakout board. We believe this is the Ultimate GPS module, so we named it that. It's got everything you want and more: -165 dBm sensitivity, 10 Hz updates, 66 channels 5V friendly design and only 20mA current draw Breadboard friendly + two mounting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
  9-DOF Absolute Orientation IMU Fusion Breakout - BNO055: A MEMS accelerometer, magnetometer and gyroscope on a single die with a high speed ARM Cortex-M0 based processor to digest all the sensor data, abstract the sensor fusion and real time requirements away, and spit out data you can use in quaternions, Euler angles or vectors.
